# Fritzing sketch BauplanRoboter (saved by Fritzing 0.9.3b)
perfboards: 1

parts:
  Bauteil1 = Arduino Mega 2560 (Rev3)
  J1 = Basic Servo
  J2 = Basic Servo
  J3 = Basic Servo
  R1 = Rotary Potentiometer (Small) [maximum_resistance=100kΩ package=THT]
  R2 = Rotary Potentiometer (Small) [maximum_resistance=100kΩ package=THT]
  Bauteil2 = Triple Axis Accelerometer Breakout - ADXL335

nets:
  N1: Bauteil1.A1, R2.leg2
  N2: Bauteil1.A2, R1.leg2
  N3: Bauteil1.A3, Bauteil2.XOUT
  N4: Bauteil1.A4, Bauteil2.YOUT
  N5: Bauteil1.A5, Bauteil2.ZOUT
  N6: Bauteil1.D13_PWM, J3.pulse
  N7: Bauteil1.D12_PWM, J2.pulse
  N8: Bauteil1.D11_PWM, J1.pulse
  5V: Bauteil1.5V, R1.wiper, R2.wiper, Bauteil2.VCC
  GND: Bauteil1.GND, J1.gnd, J2.gnd, J3.gnd, R1.leg1, R2.leg1, Bauteil2.GND
  VCC: Bauteil1.VIN, J1.vcc, J2.vcc, J3.vcc
